# Fritzing sketch motor (saved by Fritzing 0.9.3b)
breadboards: 1

parts:
  U1 = 2-Channel 5v Relay Shield [package=relay-2ch5v10a]
  Part1 = Adafruit T-Cobbler Plus [part_number="Adafruit #1989 and #2028"]
  VCC1 = Battery
  M1 = DC Motor
  U2 = 2-Channel 5v Relay Shield [package=relay-2ch5v10a]

nets (from the breadboard view):
  GND: U1.GND, Part1.GND, U2.GND
  N1: U1.IN1, Part1.GPIO21
  N2: U1.K1-In, VCC1.-
  N3: U1.K1-On, U2.K1-Off, U2.K2-On
  N4: Part1.GPIO27, U2.IN1
  +5V: Part1.+5V, U2.VCC
  N5: VCC1.+, U2.K1-On, U2.K2-Off
  N6: M1.pin_1, U2.K1-In
  N7: M1.pin_2, U2.K2-In

custom parts:
  2-Channel 5v Relay Shield: 2 Channel 5v Relay Shield w. 2x SPD-06VDC-SD-C
  Adafruit T-Cobbler Plus: The Raspberry Pi has landed on the Maker World like a 40-GPIO pinned, quad-USB ported, credit card sized bomb of DIY joy. And while you can use most of our great Model B accessories by hooking up our downgrade cable, its probably a good time to upgrade your set up and accessorize using all of the 40 pins. That's why we now carry the Assembled Adafruit Pi T-Cobbler Plus - Breakout + Cable for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
